// Logisim project MULTIPLEXER.circ as structural Verilog: 2 circuits, main circuit main
module main (
  input  I0,
  input  I1,
  input  I2,
  input  I3,
  input  inverter_A,
  input  inverter_B,
  output x
);

  wire nand_1_out, nand_2_out, nand_3_out, nand_4_out, nand_5_out, nand_6_out;

  nand nand_1 (nand_1_out, inverter_A, inverter_A);
  nand nand_2 (nand_2_out, inverter_B, inverter_B);
  nand nand_3 (nand_3_out, I0, nand_1_out, nand_2_out);
  nand nand_4 (nand_4_out, inverter_A, nand_2_out, I1);
  nand nand_5 (nand_5_out, I2, inverter_B, nand_1_out);
  nand nand_6 (nand_6_out, inverter_A, inverter_B, I3);
  nand nand_7 (x, nand_3_out, nand_4_out, nand_5_out, nand_6_out);
endmodule

module multiplexer (
  input  in_1,
  input  in_2,
  input  in_3,
  input  in_4,
  input  in_5,
  input  in_6,
  output out_7
);

  main main_1 (.I0(in_1), .I1(in_2), .I2(in_3), .I3(in_4), .inverter_A(in_5), .inverter_B(in_6), .x(out_7));
endmodule
